# Fritzing sketch doorbell (saved by Fritzing 0.9.3b)
circuit board: 5.99999cm x 8.50001cm
breadboards: 1

parts:
  ESP8266 = Adafruit HUZZAH ESP8266 [part_number="Adafruit #2471"]
  Silencer = Round Pushbutton
  MOSFET = MOSFET-NCHANNEL [package=to220v]
  R1 = Resistor [tolerance=±5% resistance=220 package=THT]
  +8V = Header 1 [package=1x01_offset]
  GND = Header 1 [package=1x01_offset]
  Pushbutton = Round Pushbutton
  DC-DC = TracoPower TSR-1 DC/DC Converter [part_number="TSR 1-2450"]
  Sel_LED = Round Pushbutton
  R2 = Resistor [tolerance=±5% resistance=220 package=THT]
  DB_GND = Header 1 [package=1x01_offset]
  DB_VCC = Header 1 [package=1x01_offset]  # not connected
  DB_SIL = Header 1 [package=1x01_offset]  # not connected
  G5V_Relay = RELAY [package=relay-g5q]  # not connected

nets:
  N1: ESP8266.VIN, R1.Pin_1, DC-DC.3, Sel_LED.leg1
  N2: ESP8266.GND, Silencer.leg0, MOSFET.S, GND.1, Pushbutton.leg0, DC-DC.2, DB_GND.1
  N3: ESP8266.GPIO16, MOSFET.G, R1.Pin_0
  N4: ESP8266.GPIO14, Silencer.leg1
  N5: ESP8266.GPIO12, Pushbutton.leg1
  N6: MOSFET.D, R2.Pin_0
  N7: +8V.1, DC-DC.1
  N8: Sel_LED.leg0, R2.Pin_1

notes:
  Doorbell button 1.0

custom parts:
  Adafruit HUZZAH ESP8266: Add Internet to your next project with an adorable, bite-sized WiFi microcontroller, at a price you like! The ESP8266 processor from Espressif is an 80 MHz microcontroller with a full WiFi front-end (both as client and access point) and TCP/IP stack with DNS support as well. While this chip has been very popular, its also been very difficult to use. Most of the low cost modules are not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
  TracoPower TSR-1 DC/DC Converter: TracoPower TSR 1-2450 DC Converter Input6.5 - 36VDC Max current 1A
